// Logisim project 16x4_bit_RAM.circ as structural Verilog: 4 circuits, main circuit sram_cell
module sram_cell (
  input  D_in,
  input  Write_En,
  input  Read_En,
  output D_out
);

  wire d_latch_1_dout;

  D_latch d_latch_1 (.Din(D_in), .WriteEN(Write_En), .Dout(d_latch_1_dout));
  assign D_out = Read_En ? d_latch_1_dout : 1'bz;  // Controlled_Buffer controlled_buffer_1
endmodule

module D_latch (
  input  Din,
  input  WriteEN,
  output Dout
);

  wire nand_1_out, nand_2_out, nand_4_out, not_1_out;

  not not_1 (not_1_out, Din);
  nand nand_1 (nand_1_out, Din, WriteEN);
  nand nand_2 (nand_2_out, WriteEN, not_1_out);
  nand nand_3 (Dout, nand_1_out, nand_4_out);
  nand nand_4 (nand_4_out, Dout, nand_2_out);
endmodule

module cell_array_4x4 (
  input  A3,
  input  A2,
  input  A1,
  input  A0,
  input  D_in,
  input  Read_En,
  input  Write_En,
  output D_out
);

  wire and_1_out, and_2_out, and_3_out, and_4_out, and_5_out, and_6_out, and_7_out, and_8_out, and_9_out,
       and_10_out, and_11_out, and_12_out, and_13_out, and_14_out, and_15_out, and_16_out, and_17_out,
       and_18_out, and_19_out, and_20_out, and_21_out, and_22_out, and_23_out, and_24_out, and_25_out,
       and_26_out, and_27_out, and_28_out, and_29_out, and_30_out, and_31_out, and_32_out, and_33_out,
       and_34_out, and_35_out, and_36_out, and_37_out, and_38_out, and_39_out, and_40_out, and_41_out,
       and_42_out, and_43_out, and_44_out, and_45_out, and_46_out, and_47_out, and_48_out, n74139_1_pin1,
       n74139_1_pin4, n74139_1_pin5, n74139_1_pin6, n74139_1_pin7, n74139_1_pin9, n74139_1_pin10,
       n74139_1_pin11, n74139_1_pin12, n74139_1_pin15, not_1_out, not_2_out, not_3_out, not_4_out, not_5_out,
       not_6_out, not_7_out, not_8_out;

  _74139 u_74139_1 (
    .pin1(n74139_1_pin1), .pin2(A2), .pin3(A3), .pin4(n74139_1_pin4), .pin5(n74139_1_pin5),
    .pin6(n74139_1_pin6), .pin7(n74139_1_pin7), .pin15(n74139_1_pin15), .pin14(A0), .pin13(A1),
    .pin12(n74139_1_pin12), .pin11(n74139_1_pin11), .pin10(n74139_1_pin10), .pin9(n74139_1_pin9));
  not not_1 (not_1_out, n74139_1_pin4);
  not not_2 (not_2_out, n74139_1_pin5);
  not not_3 (not_3_out, n74139_1_pin6);
  not not_4 (not_4_out, n74139_1_pin7);
  not not_5 (not_5_out, n74139_1_pin12);
  and and_1 (and_1_out, not_1_out, not_5_out);
  and and_2 (and_2_out, not_2_out, not_5_out);
  and and_3 (and_3_out, not_3_out, not_5_out);
  and and_4 (and_4_out, not_4_out, not_5_out);
  and and_5 (and_5_out, and_1_out, Write_En);
  and and_6 (and_6_out, and_1_out, Read_En);
  and and_7 (and_7_out, and_2_out, Write_En);
  and and_8 (and_8_out, and_2_out, Read_En);
  and and_9 (and_9_out, and_3_out, Write_En);
  and and_10 (and_10_out, and_3_out, Read_En);
  sram_cell sram_cell_1 (.D_in(D_in), .Write_En(and_5_out), .Read_En(and_6_out), .D_out(D_out));
  sram_cell sram_cell_2 (.D_in(D_in), .Write_En(and_7_out), .Read_En(and_8_out), .D_out(D_out));
  sram_cell sram_cell_3 (.D_in(D_in), .Write_En(and_9_out), .Read_En(and_10_out), .D_out(D_out));
  and and_11 (and_11_out, and_4_out, Write_En);
  sram_cell sram_cell_4 (.D_in(D_in), .Write_En(and_11_out), .Read_En(and_12_out), .D_out(D_out));
  and and_12 (and_12_out, and_4_out, Read_En);
  not not_6 (not_6_out, n74139_1_pin11);
  and and_13 (and_13_out, not_1_out, not_6_out);
  and and_14 (and_14_out, not_2_out, not_6_out);
  and and_15 (and_15_out, not_3_out, not_6_out);
  and and_16 (and_16_out, not_4_out, not_6_out);
  and and_17 (and_17_out, and_13_out, Write_En);
  and and_18 (and_18_out, and_13_out, Read_En);
  and and_19 (and_19_out, and_14_out, Write_En);
  and and_20 (and_20_out, and_14_out, Read_En);
  and and_21 (and_21_out, and_15_out, Write_En);
  and and_22 (and_22_out, and_15_out, Read_En);
  and and_23 (and_23_out, and_16_out, Write_En);
  and and_24 (and_24_out, and_16_out, Read_En);
  sram_cell sram_cell_5 (.D_in(D_in), .Write_En(and_17_out), .Read_En(and_18_out), .D_out(D_out));
  sram_cell sram_cell_6 (.D_in(D_in), .Write_En(and_19_out), .Read_En(and_20_out), .D_out(D_out));
  sram_cell sram_cell_7 (.D_in(D_in), .Write_En(and_21_out), .Read_En(and_22_out), .D_out(D_out));
  sram_cell sram_cell_8 (.D_in(D_in), .Write_En(and_23_out), .Read_En(and_24_out), .D_out(D_out));
  not not_7 (not_7_out, n74139_1_pin10);
  and and_25 (and_25_out, not_1_out, not_7_out);
  and and_26 (and_26_out, not_2_out, not_7_out);
  and and_27 (and_27_out, not_3_out, not_7_out);
  and and_28 (and_28_out, not_4_out, not_7_out);
  and and_29 (and_29_out, and_25_out, Write_En);
  and and_30 (and_30_out, and_25_out, Read_En);
  and and_31 (and_31_out, and_26_out, Write_En);
  and and_32 (and_32_out, and_26_out, Read_En);
  and and_33 (and_33_out, and_27_out, Write_En);
  and and_34 (and_34_out, and_27_out, Read_En);
  sram_cell sram_cell_9 (.D_in(D_in), .Write_En(and_29_out), .Read_En(and_30_out), .D_out(D_out));
  sram_cell sram_cell_10 (.D_in(D_in), .Write_En(and_31_out), .Read_En(and_32_out), .D_out(D_out));
  sram_cell sram_cell_11 (.D_in(D_in), .Write_En(and_33_out), .Read_En(and_34_out), .D_out(D_out));
  and and_35 (and_35_out, and_28_out, Write_En);
  sram_cell sram_cell_12 (.D_in(D_in), .Write_En(and_35_out), .Read_En(and_36_out), .D_out(D_out));
  and and_36 (and_36_out, and_28_out, Read_En);
  not not_8 (not_8_out, n74139_1_pin9);
  and and_37 (and_37_out, not_1_out, not_8_out);
  and and_38 (and_38_out, not_2_out, not_8_out);
  and and_39 (and_39_out, not_3_out, not_8_out);
  and and_40 (and_40_out, not_4_out, not_8_out);
  and and_41 (and_41_out, and_37_out, Write_En);
  and and_42 (and_42_out, and_37_out, Read_En);
  and and_43 (and_43_out, and_38_out, Write_En);
  and and_44 (and_44_out, and_38_out, Read_En);
  and and_45 (and_45_out, and_39_out, Write_En);
  and and_46 (and_46_out, and_39_out, Read_En);
  and and_47 (and_47_out, and_40_out, Write_En);
  and and_48 (and_48_out, and_40_out, Read_En);
  sram_cell sram_cell_13 (.D_in(D_in), .Write_En(and_41_out), .Read_En(and_42_out), .D_out(D_out));
  sram_cell sram_cell_14 (.D_in(D_in), .Write_En(and_43_out), .Read_En(and_44_out), .D_out(D_out));
  sram_cell sram_cell_15 (.D_in(D_in), .Write_En(and_45_out), .Read_En(and_46_out), .D_out(D_out));
  sram_cell sram_cell_16 (.D_in(D_in), .Write_En(and_47_out), .Read_En(and_48_out), .D_out(D_out));
  // also tied to GND on the sheet: {n74139_1_pin1, n74139_1_pin15}

  // Notes on the sheet:
  //   D_out: pull=down
endmodule

module RAM_block_16x4 (
  input  D3,
  input  D2,
  input  D1,
  input  D0,
  input  READorWRITE,
  input  A3,
  input  A2,
  input  A1,
  input  A0,
  output D3_Out,
  output D2_Out,
  output D1_Out,
  output D0_Out
);

  wire not_1_out;

  not not_1 (not_1_out, READorWRITE);
  cell_array_4x4 cell_array_4x4_1 (
    .A3(A3), .A2(A2), .A1(A1), .A0(A0), .D_in(D3), .Read_En(not_1_out), .Write_En(READorWRITE), .D_out(D3_Out));
  cell_array_4x4 cell_array_4x4_2 (
    .A3(A3), .A2(A2), .A1(A1), .A0(A0), .D_in(D2), .Read_En(not_1_out), .Write_En(READorWRITE), .D_out(D2_Out));
  cell_array_4x4 cell_array_4x4_3 (
    .A3(A3), .A2(A2), .A1(A1), .A0(A0), .D_in(D1), .Read_En(not_1_out), .Write_En(READorWRITE), .D_out(D1_Out));
  cell_array_4x4 cell_array_4x4_4 (
    .A3(A3), .A2(A2), .A1(A1), .A0(A0), .D_in(D0), .Read_En(not_1_out), .Write_En(READorWRITE), .D_out(D0_Out));

  // Notes on the sheet:
  //   When 0=Read
  //   When 1=Write
endmodule
