// Logisim project 4_bit_CPU.circ as structural Verilog: 2 circuits, main circuit Clk
module Clk (
  input  AutoClk,
  input  Sel,
  input  ManClk,
  input  Hlt,
  output out_5
);

  wire and_1_out, and_2_out, not_1_out, not_2_out, or_1_out;

  not not_1 (not_1_out, Hlt);
  and and_1 (and_1_out, AutoClk, Sel);
  not not_2 (not_2_out, Sel);
  and and_2 (and_2_out, not_2_out, ManClk);
  or or_1 (or_1_out, and_1_out, and_2_out);
  and and_3 (out_5, or_1_out, not_1_out);
endmodule

module CPU (
  input  CLEAR,
  input  Sel,
  input  HLT,
  input  in_4,
  input  in_5,
  input  in_6,
  input  in_7,
  output out_8,
  output out_9,
  output out_10,
  output out_11
);

  wire alu_1_c4, alu_1_f0, alu_1_f1, alu_1_f2, alu_1_f3, AutoClk_out, clk_1_out_5, cout_1_cflag,
       data_mux_1_a0, data_mux_1_a1, data_mux_1_a2, data_mux_1_a3, halt_1_haltout, In_Ready_out,
       in_register_1_a0, in_register_1_a1, in_register_1_a2, in_register_1_a3, instruction_register_1_b0,
       instruction_register_1_b1, instruction_register_1_b2, instruction_register_1_b3, main_1_cin,
       main_1_co_w_en, main_1_halt, main_1_halt_w_en, main_1_in_w_en, main_1_ir_w_en, main_1_m, main_1_m0,
       main_1_m1, main_1_mar_w_en, main_1_mdin_w_en, main_1_mdr_w_en, main_1_out_o_en, main_1_pc_inc,
       main_1_pc_load, main_1_rega_w_en, main_1_regb_w_en, main_1_rom_write, main_1_s0, main_1_s1, main_1_s2,
       main_1_s3, ManClk_out, memory_address_register_1_a0, memory_address_register_1_a1,
       memory_address_register_1_a2, memory_address_register_1_a3, memory_data_in_register_1_d0,
       memory_data_in_register_1_d1, memory_data_in_register_1_d2, memory_data_in_register_1_d3,
       memory_data_register_1_ab0, memory_data_register_1_ab1, memory_data_register_1_ab2,
       memory_data_register_1_ab3, not_1_out, or_1_out, ram_block_16x4_1_d0_out, ram_block_16x4_1_d1_out,
       ram_block_16x4_1_d2_out, ram_block_16x4_1_d3_out, reg_a_1_aq0, reg_a_1_aq1, reg_a_1_aq2, reg_a_1_aq3,
       reg_b_1_bq0, reg_b_1_bq1, reg_b_1_bq2, reg_b_1_bq3;
  wire [3:0] main_1_out_13, pc_1_q0, rom_1_data;

  PC pc_1 (
    .CLR(CLEAR), .Clk(clk_1_out_5), .i0(rom_1_data[0]), .i1(rom_1_data[1]), .i2(rom_1_data[2]),
    .i3(rom_1_data[3]), .LOAD(main_1_pc_load), .INC(main_1_pc_inc), .q0(pc_1_q0[0]), .q1(pc_1_q0[1]),
    .q2(pc_1_q0[2]), .q3(pc_1_q0[3]));
  halt halt_1 (
    .haltin(main_1_halt), .halt_Wen(main_1_halt_w_en), .Clk(clk_1_out_5), .Clear(CLEAR),
    .haltout(halt_1_haltout));
  Clock AutoClk (.out(AutoClk_out));
  Button ManClk (.out(ManClk_out));
  ROM #(.addrWidth(4), .dataWidth(4)) rom_1 (.addr(pc_1_q0), .data(rom_1_data));
  Clk clk_1 (.Sel(Sel), .AutoClk(AutoClk_out), .ManClk(ManClk_out), .Hlt(or_1_out), .out_5(clk_1_out_5));
  or or_1 (or_1_out, halt_1_haltout, HLT);
  Button In_Ready (.out(In_Ready_out));
  Instruction_Register instruction_register_1 (
    .Wrie_En(main_1_ir_w_en), .i0(rom_1_data[0]), .i1(rom_1_data[1]), .i2(rom_1_data[2]), .i3(rom_1_data[3]),
    .Clk(clk_1_out_5), .b0(instruction_register_1_b0), .b1(instruction_register_1_b1),
    .b2(instruction_register_1_b2), .b3(instruction_register_1_b3));
  Hex_Digit_Display #(.decimalPoint("false")) hex_digit_display_1 (.value({in_4, in_5, in_6, in_7}));
  In_Register in_register_1 (
    .Write_En(main_1_in_w_en), .i0(in_7), .i1(in_6), .i2(in_5), .i3(in_4), .Clk(clk_1_out_5),
    .a0(in_register_1_a0), .a1(in_register_1_a1), .a2(in_register_1_a2), .a3(in_register_1_a3));
  Hex_Digit_Display #(.decimalPoint("false")) hex_digit_display_2 (.value(main_1_out_13));
  not not_1 (not_1_out, clk_1_out_5);
  Control_Unit_main main_1 (
    .i3(instruction_register_1_b3), .i2(instruction_register_1_b2), .i1(instruction_register_1_b1),
    .I0(instruction_register_1_b0), .Cout(cout_1_cflag), .invCLK(not_1_out), .Clr(CLEAR),
    .IN_READY(In_Ready_out), .a3(reg_a_1_aq3), .a2(reg_a_1_aq2), .a1(reg_a_1_aq1), .a0(reg_a_1_aq0),
    .M(main_1_m), .S3(main_1_s3), .S2(main_1_s2), .S1(main_1_s1), .S0(main_1_s0), .Cin(main_1_cin),
    .IN_W_En(main_1_in_w_en), .M1(main_1_m1), .OUT_O_En(main_1_out_o_en), .M0(main_1_m0),
    .RegB_W_En(main_1_regb_w_en), .ROM_Write(main_1_rom_write), .MDIn_W_En(main_1_mdin_w_en),
    .Co_W_En(main_1_co_w_en), .MDR_W_En(main_1_mdr_w_en), .HALT(main_1_halt), .RegA_W_En(main_1_rega_w_en),
    .MAR_W_En(main_1_mar_w_en), .PC_INC(main_1_pc_inc), .out_13(main_1_out_13), .IR_W_En(main_1_ir_w_en),
    .PC_LOAD(main_1_pc_load), .HALT_W_En(main_1_halt_w_en));
  Out_Register out_register_1 (
    .Out_En(main_1_out_o_en), .a0(reg_a_1_aq0), .a1(reg_a_1_aq1), .a2(reg_a_1_aq2), .a3(reg_a_1_aq3),
    .Clk(clk_1_out_5), .o0(out_11), .o1(out_10), .o2(out_9), .o3(out_8));
  data_mux data_mux_1 (
    .alu0(alu_1_f0), .alu1(alu_1_f1), .alu2(alu_1_f2), .alu3(alu_1_f3), .in0(in_register_1_a0),
    .in1(in_register_1_a1), .in2(in_register_1_a2), .in3(in_register_1_a3),
    .ram0(memory_data_register_1_ab0), .ram1(memory_data_register_1_ab1), .ram2(memory_data_register_1_ab2),
    .ram3(memory_data_register_1_ab3), .M1(main_1_m1), .M0(main_1_m0), .a0(data_mux_1_a0),
    .a1(data_mux_1_a1), .a2(data_mux_1_a2), .a3(data_mux_1_a3));
  Reg_A reg_a_1 (
    .Write_En(main_1_rega_w_en), .Ai0(data_mux_1_a0), .Ai1(data_mux_1_a1), .Ai2(data_mux_1_a2),
    .Ai3(data_mux_1_a3), .Clk(clk_1_out_5), .Aq0(reg_a_1_aq0), .Aq1(reg_a_1_aq1), .Aq2(reg_a_1_aq2),
    .Aq3(reg_a_1_aq3));
  Hex_Digit_Display #(.decimalPoint("false")) hex_digit_display_3 (.value({out_8, out_9, out_10, out_11}));
  Memory_Address_Register memory_address_register_1 (
    .Write_En(main_1_mar_w_en), .b0(rom_1_data[0]), .b1(rom_1_data[1]), .b2(rom_1_data[2]),
    .b3(rom_1_data[3]), .Clk(clk_1_out_5), .A0(memory_address_register_1_a0),
    .A1(memory_address_register_1_a1), .A2(memory_address_register_1_a2), .A3(memory_address_register_1_a3));
  ALU alu_1 (
    .b0(reg_b_1_bq0), .a1(reg_a_1_aq1), .a0(reg_a_1_aq0), .b1(reg_b_1_bq1), .s3(main_1_s3), .a2(reg_a_1_aq2),
    .s2(main_1_s2), .b2(reg_b_1_bq2), .s1(main_1_s1), .a3(reg_a_1_aq3), .s0(main_1_s0), .b3(reg_b_1_bq3),
    .c0(main_1_cin), .M(main_1_m), .c4(alu_1_c4), .f0(alu_1_f0), .f1(alu_1_f1), .f2(alu_1_f2), .f3(alu_1_f3));  // open: aisequaltob
  Memory_Data_Register memory_data_register_1 (
    .Write_En(main_1_mdr_w_en), .d0(ram_block_16x4_1_d0_out), .d1(ram_block_16x4_1_d1_out),
    .d2(ram_block_16x4_1_d2_out), .d3(ram_block_16x4_1_d3_out), .Clk(clk_1_out_5),
    .ab0(memory_data_register_1_ab0), .ab1(memory_data_register_1_ab1), .ab2(memory_data_register_1_ab2),
    .ab3(memory_data_register_1_ab3));
  RAM_block_16x4 ram_block_16x4_1 (
    .READorWRITE(main_1_rom_write), .D3(memory_data_in_register_1_d3), .D2(memory_data_in_register_1_d2),
    .D1(memory_data_in_register_1_d1), .D0(memory_data_in_register_1_d0), .A3(memory_address_register_1_a3),
    .A2(memory_address_register_1_a2), .A1(memory_address_register_1_a1), .A0(memory_address_register_1_a0),
    .D3_Out(ram_block_16x4_1_d3_out), .D2_Out(ram_block_16x4_1_d2_out), .D1_Out(ram_block_16x4_1_d1_out),
    .D0_Out(ram_block_16x4_1_d0_out));
  Memory_Data_In_Register memory_data_in_register_1 (
    .Write_En(main_1_mdin_w_en), .a0(reg_a_1_aq0), .a1(reg_a_1_aq1), .a2(reg_a_1_aq2), .a3(reg_a_1_aq3),
    .Clk(clk_1_out_5), .d0(memory_data_in_register_1_d0), .d1(memory_data_in_register_1_d1),
    .d2(memory_data_in_register_1_d2), .d3(memory_data_in_register_1_d3));
  Reg_B reg_b_1 (
    .Write_En(main_1_regb_w_en), .Bi0(memory_data_register_1_ab0), .Bi1(memory_data_register_1_ab1),
    .Bi2(memory_data_register_1_ab2), .Bi3(memory_data_register_1_ab3), .Clk(clk_1_out_5), .Bq0(reg_b_1_bq0),
    .Bq1(reg_b_1_bq1), .Bq2(reg_b_1_bq2), .Bq3(reg_b_1_bq3));
  Cout cout_1 (.Co(alu_1_c4), .W_En(main_1_co_w_en), .Clk(clk_1_out_5), .Clear(CLEAR), .Cflag(cout_1_cflag));

  // Notes on the sheet:
  //   contents of rom_1 (hex, n*v repeats v):
  //   c 7 1 c 6 1 4 e 2
  //   INPUT
  //   STATE
  //   OUTPUT
endmodule
