// Logisim project 74181_ALU.circ as structural Verilog: 1 circuit, main circuit ALU
module ALU (
  input  b1,
  input  b2,
  input  b3,
  input  a1,
  input  a2,
  input  a3,
  input  c0,
  input  M,
  input  a0,
  input  b0,
  input  s3,
  input  s2,
  input  s1,
  input  s0,
  output aisequaltob,
  output c4,
  output f0,
  output f1,
  output f2,
  output f3
);

  wire n74181_1_p15;

  // _74181 74181_1: pin names not known; wires that end beside it: b0, a1, a0, b1, s3, a2, s2, b2, s1, a3, s0, b3, c0, M, n74181_1_p15, f0, f1, aisequaltob, f2, f3
  not not_1 (c4, n74181_1_p15);
endmodule
