// Logisim project Control_Unit.circ as structural Verilog: 1 circuit, main circuit main
module main (
  input  i3,
  input  i2,
  input  i1,
  input  I0,
  input  invCLK,
  input  IN_READY,
  input  Cout,
  input  Clr,
  input  a3,
  input  a2,
  input  a1,
  input  a0,
  output [3:0] out_13,
  output M,
  output S3,
  output S2,
  output S1,
  output S0,
  output Cin,
  output M1,
  output M0,
  output HALT,
  output MDIn_W_En,
  output IR_W_En,
  output MDR_W_En,
  output RegB_W_En,
  output HALT_W_En,
  output Co_W_En,
  output PC_LOAD,
  output MAR_W_En,
  output ROM_Write,
  output PC_INC,
  output RegA_W_En,
  output IN_W_En,
  output OUT_O_En
);

  wire and_1_out, and_2_out, and_3_out, and_4_out, and_5_out, and_6_out, and_7_out, and_8_out, and_9_out,
       and_10_out, and_11_out, and_12_out, and_13_out, and_22_out, and_23_out, and_25_out, and_26_out,
       and_27_out, n74138_1_pin6, n74138_1_pin7, n74138_1_pin9, n74138_1_pin10, n74138_1_pin11,
       n74138_1_pin12, n74138_1_pin13, n74138_1_pin14, n74138_1_pin15, n74138_2_pin4, n74138_2_pin7,
       n74138_2_pin9, n74138_2_pin10, n74138_2_pin11, n74138_2_pin12, n74138_2_pin13, n74138_2_pin14,
       n74138_2_pin15, n74138_3_pin6, n74138_3_pin7, n74138_3_pin9, n74138_3_pin10, n74138_3_pin11,
       n74138_3_pin12, n74138_3_pin13, n74138_3_pin14, n74138_3_pin15, n74163_1_pin3, n74163_1_pin7,
       n74163_1_pin9, nor_1_out, nor_2_out, not_1_out, not_2_out, not_3_out, not_5_out, not_6_out, not_7_out,
       not_8_out, not_9_out, not_10_out, not_11_out, not_12_out, not_13_out, not_14_out, not_15_out,
       not_16_out, not_18_out, not_19_out, not_20_out, not_21_out, not_22_out, not_23_out, not_25_out,
       not_26_out, not_27_out, not_28_out, not_29_out, or_2_out, or_5_out, or_6_out, or_7_out, or_9_out,
       or_10_out, or_11_out, or_12_out, or_13_out, or_14_out;

  not not_1 (not_1_out, or_2_out);
  _74163 u_74163_1 (
    .pin1(not_1_out), .pin2(invCLK), .pin3(n74163_1_pin3), .pin4(n74163_1_pin3), .pin5(n74163_1_pin3),
    .pin6(n74163_1_pin3), .pin7(n74163_1_pin7), .pin14(out_13[0]), .pin13(out_13[1]), .pin12(out_13[2]),
    .pin11(out_13[3]), .pin10(n74163_1_pin7), .pin9(n74163_1_pin9));  // open: pin15
  not not_2 (not_2_out, IN_W_En);
  or or_1 (n74163_1_pin7, not_2_out, IN_READY);
  or or_2 (or_2_out, and_1_out, and_2_out, Clr, and_3_out, and_4_out);
  or or_3 (PC_INC, not_5_out, and_7_out, and_10_out, and_8_out, and_9_out);
  not not_3 (not_3_out, n74138_1_pin6);
  and and_1 (and_1_out, or_5_out, not_7_out);
  and and_2 (and_2_out, or_6_out, not_8_out);
  and and_3 (and_3_out, or_7_out, not_10_out);
  and and_4 (and_4_out, not_28_out, not_11_out);
  or or_4 (PC_LOAD, and_5_out, and_6_out);
  _74138 u_74138_1 (
    .pin1(out_13[0]), .pin2(out_13[1]), .pin3(out_13[2]), .pin4(not_3_out), .pin5(not_3_out),
    .pin6(n74138_1_pin6), .pin7(n74138_1_pin7), .pin15(n74138_1_pin15), .pin14(n74138_1_pin14),
    .pin13(n74138_1_pin13), .pin12(n74138_1_pin12), .pin11(n74138_1_pin11), .pin10(n74138_1_pin10),
    .pin9(n74138_1_pin9));
  or or_5 (or_5_out, not_14_out, not_15_out, not_16_out, not_18_out, not_20_out, not_21_out, not_26_out, not_27_out);
  or or_6 (or_6_out, not_29_out, not_25_out, not_19_out, M0);
  or or_7 (or_7_out, M1, not_23_out, not_22_out);
  and and_5 (and_5_out, not_20_out, not_6_out);
  and and_6 (and_6_out, not_19_out, not_6_out, nor_1_out);
  and and_7 (and_7_out, M1, not_7_out);
  and and_8 (and_8_out, not_23_out, not_7_out);
  and and_9 (and_9_out, not_19_out, not_7_out, not_12_out);
  and and_10 (and_10_out, not_22_out, not_8_out);
  nor nor_1 (nor_1_out, a3, a2, a1, a0);
  not not_4 (IR_W_En, n74138_1_pin15);
  not not_5 (not_5_out, n74138_1_pin14);
  not not_6 (not_6_out, n74138_1_pin13);
  not not_7 (not_7_out, n74138_1_pin12);
  not not_8 (not_8_out, n74138_1_pin11);
  not not_9 (not_9_out, n74138_1_pin10);
  not not_10 (not_10_out, n74138_1_pin9);
  not not_11 (not_11_out, n74138_1_pin7);
  or or_8 (HALT_W_En, and_12_out, and_11_out);
  not not_12 (not_12_out, nor_1_out);
  and and_11 (and_11_out, or_9_out, not_7_out);
  and and_12 (and_12_out, not_27_out, not_6_out);
  or or_9 (or_9_out, not_29_out, not_25_out);
  and and_13 (and_13_out, I0, i3);
  not not_13 (not_13_out, i1);
  and and_14 (S0, i2, not_13_out, or_10_out);
  nor nor_2 (nor_2_out, I0, i3);
  or or_10 (or_10_out, and_13_out, nor_2_out);
  and and_15 (Cin, S0, i2);
  and and_16 (IN_W_En, not_6_out, M0);
  and and_17 (OUT_O_En, not_6_out, not_15_out);
  not not_14 (not_14_out, n74138_2_pin7);
  not not_15 (not_15_out, n74138_2_pin9);
  not not_16 (not_16_out, n74138_2_pin10);
  not not_17 (M0, n74138_2_pin11);
  not not_18 (not_18_out, n74138_2_pin12);
  not not_19 (not_19_out, n74138_2_pin13);
  _74138 u_74138_2 (
    .pin1(I0), .pin2(i1), .pin3(i2), .pin4(n74138_2_pin4), .pin5(n74138_2_pin4), .pin6(i3),
    .pin7(n74138_2_pin7), .pin15(n74138_2_pin15), .pin14(n74138_2_pin14), .pin13(n74138_2_pin13),
    .pin12(n74138_2_pin12), .pin11(n74138_2_pin11), .pin10(n74138_2_pin10), .pin9(n74138_2_pin9));
  not not_20 (not_20_out, n74138_2_pin14);
  not not_21 (not_21_out, n74138_2_pin15);
  not not_22 (not_22_out, n74138_3_pin7);
  not not_23 (not_23_out, n74138_3_pin9);
  not not_24 (M1, n74138_3_pin10);
  not not_25 (not_25_out, n74138_3_pin11);
  not not_26 (not_26_out, n74138_3_pin12);
  not not_27 (not_27_out, n74138_3_pin13);
  _74138 u_74138_3 (
    .pin1(I0), .pin2(i1), .pin3(i2), .pin4(i3), .pin5(n74138_2_pin4), .pin6(n74138_3_pin6),
    .pin7(n74138_3_pin7), .pin15(n74138_3_pin15), .pin14(n74138_3_pin14), .pin13(n74138_3_pin13),
    .pin12(n74138_3_pin12), .pin11(n74138_3_pin11), .pin10(n74138_3_pin10), .pin9(n74138_3_pin9));
  not not_28 (not_28_out, n74138_3_pin14);
  not not_29 (not_29_out, n74138_3_pin15);
  or or_11 (or_11_out, M1, not_23_out);
  and and_18 (RegB_W_En, not_23_out, not_9_out);
  or or_12 (or_12_out, not_29_out, not_25_out);
  and and_19 (MDIn_W_En, not_6_out, not_22_out);
  and and_20 (MDR_W_En, or_11_out, not_8_out);
  and and_21 (Co_W_En, or_12_out, not_6_out);
  or or_13 (or_13_out, M1, not_23_out);
  and and_22 (and_22_out, or_13_out, not_6_out);
  and and_23 (and_23_out, not_22_out, not_7_out);
  and and_24 (ROM_Write, not_22_out, not_8_out);
  or or_14 (or_14_out, not_29_out, not_26_out, not_25_out, not_21_out, not_18_out, not_16_out, not_14_out);
  or or_15 (HALT, not_27_out, Cout);
  or or_16 (MAR_W_En, and_22_out, and_23_out);
  and and_25 (and_25_out, or_14_out, not_6_out);
  and and_26 (and_26_out, M0, not_7_out);
  and and_27 (and_27_out, M1, not_9_out);
  or or_17 (RegA_W_En, and_25_out, and_26_out, and_27_out);

  assign M = i3;
  assign S1 = I0;
  assign S2 = i1;
  assign S3 = i2;
  // also tied to GND on the sheet: {n74163_1_pin3, n74138_2_pin4}
  // also tied to VCC on the sheet: {n74163_1_pin9, n74138_1_pin6, n74138_3_pin6}

  // Notes on the sheet:
  //   T_RESET
  //   PC_INC
  //   PC_LOAD
  //   HALT_W_En
  //   T7
  //   T6
  //   T5
  //   T4
  //   T3
  //   T2
  //   T1
  //   T0
endmodule
