// Logisim project MUX.circ as structural Verilog: 1 circuit, main circuit data_mux
module data_mux (
  input  alu0,
  input  alu1,
  input  alu2,
  input  alu3,
  input  in0,
  input  in1,
  input  in2,
  input  in3,
  input  ram0,
  input  ram1,
  input  ram2,
  input  M1,
  input  M0,
  input  ram3,
  output a0,
  output a1,
  output a2,
  output a3
);

  Multiplexer #(.select(2), .width(4)) multiplexer_1 (
    .in0({alu3, alu2, alu1, alu0}), .in1({in3, in2, in1, in0}), .in2({ram3, ram2, ram1, ram0}),
    .out({a3, a2, a1, a0}), .sel({M1, M0}));  // open: in3
endmodule
