// Logisim project Program_Counter.circ as structural Verilog: 1 circuit, main circuit PC
module PC (
  input  LOAD,
  input  INC,
  input  CLR,
  input  Clk,
  input  i0,
  input  i1,
  input  i2,
  input  i3,
  output q0,
  output q1,
  output q2,
  output q3
);

  wire n74161_1_pin1, n74161_1_pin9;

  _74161 u_74161_1 (
    .pin1(n74161_1_pin1), .pin2(Clk), .pin3(i0), .pin4(i1), .pin5(i2), .pin6(i3), .pin7(INC), .pin14(q0),
    .pin13(q1), .pin12(q2), .pin11(q3), .pin10(INC), .pin9(n74161_1_pin9));  // open: pin15
  not not_1 (n74161_1_pin1, CLR);
  not not_2 (n74161_1_pin9, LOAD);
endmodule
