// Logisim project Registers.circ as structural Verilog: 11 circuits, main circuit Reg_A
module Reg_A (
  input  Ai3,
  input  Ai2,
  input  Ai1,
  input  Ai0,
  input  Write_En,
  input  Clk,
  output Aq0,
  output Aq1,
  output Aq2,
  output Aq3
);

  Register_4_bit register_4_bit_1 (
    .Write_En(Write_En), .D0(Ai0), .D1(Ai1), .D2(Ai2), .D3(Ai3), .CLK(Clk), .Out_En(1'b1), .Q0(Aq0),
    .Q1(Aq1), .Q2(Aq2), .Q3(Aq3));
endmodule

module Register_4_bit (
  input  D0,
  input  D1,
  input  D2,
  input  Write_En,
  input  D3,
  input  CLK,
  input  Out_En,
  output Q0,
  output Q1,
  output Q2,
  output Q3
);

  wire and_1_out, and_2_out, and_3_out, and_4_out, and_5_out, and_6_out, and_7_out, and_8_out, d_ff_1_q,
       d_ff_1_qn, d_ff_2_q, d_ff_2_qn, d_ff_3_q, d_ff_3_qn, d_ff_4_q, d_ff_4_qn, not_1_out, or_1_out,
       or_2_out, or_3_out, or_4_out;

  not not_1 (not_1_out, Write_En);
  and and_1 (and_1_out, d_ff_1_q, not_1_out);
  or or_1 (or_1_out, and_1_out, and_2_out);
  and and_2 (and_2_out, D0, Write_En);
  and and_3 (and_3_out, d_ff_2_q, not_1_out);
  or or_2 (or_2_out, and_3_out, and_4_out);
  and and_4 (and_4_out, D1, Write_En);
  and and_5 (and_5_out, d_ff_3_q, not_1_out);
  or or_3 (or_3_out, and_5_out, and_6_out);
  and and_6 (and_6_out, D2, Write_En);
  and and_7 (and_7_out, d_ff_4_q, not_1_out);
  or or_4 (or_4_out, and_7_out, and_8_out);
  and and_8 (and_8_out, D3, Write_En);
  D_Flip_Flop d_ff_1 (.D(or_1_out), .clk(CLK), .Q(d_ff_1_q), .Qn(d_ff_1_qn));  // open: preset, reset
  D_Flip_Flop d_ff_2 (.D(or_2_out), .clk(CLK), .Q(d_ff_2_q), .Qn(d_ff_2_qn));  // open: preset, reset
  D_Flip_Flop d_ff_3 (.D(or_3_out), .clk(CLK), .Q(d_ff_3_q), .Qn(d_ff_3_qn));  // open: preset, reset
  D_Flip_Flop d_ff_4 (.D(or_4_out), .clk(CLK), .Q(d_ff_4_q), .Qn(d_ff_4_qn));  // open: preset, reset
  assign Q0 = Out_En ? ~d_ff_1_qn : 1'bz;  // Controlled_Inverter controlled_inverter_1
  assign Q1 = Out_En ? ~d_ff_2_qn : 1'bz;  // Controlled_Inverter controlled_inverter_2
  assign Q2 = Out_En ? ~d_ff_3_qn : 1'bz;  // Controlled_Inverter controlled_inverter_3
  assign Q3 = Out_En ? ~d_ff_4_qn : 1'bz;  // Controlled_Inverter controlled_inverter_4
endmodule

module Reg_B (
  input  Bi0,
  input  Bi1,
  input  Bi2,
  input  Bi3,
  input  Write_En,
  input  Clk,
  output Bq3,
  output Bq2,
  output Bq1,
  output Bq0
);

  Register_4_bit register_4_bit_1 (
    .Write_En(Write_En), .D0(Bi0), .D1(Bi1), .D2(Bi2), .D3(Bi3), .CLK(Clk), .Out_En(1'b1), .Q0(Bq0),
    .Q1(Bq1), .Q2(Bq2), .Q3(Bq3));
endmodule

module Memory_Address_Register (
  input  b0,
  input  b1,
  input  b2,
  input  b3,
  input  Write_En,
  input  Clk,
  output A0,
  output A1,
  output A2,
  output A3
);

  Register_4_bit register_4_bit_1 (
    .Write_En(Write_En), .D0(b0), .D1(b1), .D2(b2), .D3(b3), .CLK(Clk), .Out_En(1'b1), .Q0(A0), .Q1(A1),
    .Q2(A2), .Q3(A3));
endmodule

module Instruction_Register (
  input  i0,
  input  i1,
  input  i2,
  input  i3,
  input  Wrie_En,
  input  Clk,
  output b0,
  output b1,
  output b2,
  output b3
);

  Register_4_bit register_4_bit_1 (
    .Write_En(Wrie_En), .D0(i0), .D1(i1), .D2(i2), .D3(i3), .CLK(Clk), .Out_En(1'b1), .Q0(b0), .Q1(b1),
    .Q2(b2), .Q3(b3));
endmodule

module Memory_Data_Register (
  input  d0,
  input  d1,
  input  d2,
  input  d3,
  input  Write_En,
  input  Clk,
  output ab0,
  output ab1,
  output ab2,
  output ab3
);

  Register_4_bit register_4_bit_1 (
    .Write_En(Write_En), .D0(d0), .D1(d1), .D2(d2), .D3(d3), .CLK(Clk), .Out_En(1'b1), .Q0(ab0), .Q1(ab1),
    .Q2(ab2), .Q3(ab3));
endmodule

module Memory_Data_In_Register (
  input  a0,
  input  a1,
  input  a2,
  input  a3,
  input  Write_En,
  input  Clk,
  output d0,
  output d1,
  output d2,
  output d3
);

  Register_4_bit register_4_bit_1 (
    .Write_En(Write_En), .D0(a0), .D1(a1), .D2(a2), .D3(a3), .CLK(Clk), .Out_En(1'b1), .Q0(d0), .Q1(d1),
    .Q2(d2), .Q3(d3));
endmodule

module In_Register (
  input  i0,
  input  i1,
  input  i2,
  input  i3,
  input  Write_En,
  input  Clk,
  output a0,
  output a1,
  output a2,
  output a3
);

  Register_4_bit register_4_bit_1 (
    .Write_En(Write_En), .D0(i0), .D1(i1), .D2(i2), .D3(i3), .CLK(Clk), .Out_En(1'b1), .Q0(a0), .Q1(a1),
    .Q2(a2), .Q3(a3));
endmodule

module Out_Register (
  input  a0,
  input  a1,
  input  a2,
  input  a3,
  input  Out_En,
  input  Clk,
  output o0,
  output o1,
  output o2,
  output o3
);

  Register_4_bit register_4_bit_1 (
    .Write_En(Out_En), .D0(a0), .D1(a1), .D2(a2), .D3(a3), .CLK(Clk), .Out_En(1'b1), .Q0(o0), .Q1(o1),
    .Q2(o2), .Q3(o3));
endmodule

module halt (
  input  haltin,
  input  halt_Wen,
  input  Clk,
  input  Clear,
  output haltout
);

  Register #(.width(1)) register_1 (.D(haltin), .en(halt_Wen), .clk(Clk), .Q(haltout), .clr(Clear));
endmodule

module Cout (
  input  Co,
  input  W_En,
  input  Clk,
  input  Clear,
  output Cflag
);

  Register #(.width(1)) register_1 (.D(Co), .en(W_En), .clk(Clk), .Q(Cflag), .clr(Clear));
endmodule
